# Fritzing sketch panorama (saved by Fritzing 0.9.2b)
breadboards: 1

parts:
  Part1 = Arduino Uno (Rev3)
  LED1 = RGB LED (com. cathode, rgb) [package="5 mm [THT]"]

nets:
  N1: Part1.D11_PWM/MOSI, LED1.red_anode
  N2: Part1.D12/MISO, LED1.green_anode
  N3: Part1.D13/SCK, LED1.blue_anode
  N4: Part1.GND, LED1.common_cathode

// code stored in the sketch: sketch.ino
/**
 * By Jesse Talavera-Greenberg
 * Listening to: Uncontrollable Urge, by DEVO
 */

const byte RED_PIN = 13;
const byte GREEN_PIN = 12;
const byte BLUE_PIN = 11;

void setup() {
  pinMode(RED_PIN, OUTPUT); 
  pinMode(GREEN_PIN, OUTPUT); 
  pinMode(BLUE_PIN, OUTPUT); 
}

void loop() {
	for (byte i = 0; i < 8; ++i) {
		digitalWrite(RED_PIN, i & 0b001 ? HIGH : LOW);
		digitalWrite(GREEN_PIN, i & 0b010 ? HIGH : LOW);
		digitalWrite(BLUE_PIN, i & 0b100 ? HIGH : LOW);
		delay(500);
	}
}
